# Fritzing sketch PCBLayout (saved by Fritzing 0.9.3b)
circuit board: 8.46667cm x 5.64444cm
breadboards: 1

parts:
  Part1 = Arduino Mega 2560 (Rev3)
  Pololu_A1 = Pololu A4988 [package=SO16]
  Pololu_A2 = Pololu A4988 [package=SO16]
  C1 = Electrolytic Capacitor [capacitance=1µF package="100 mil [THT, electrolytic]"]
  C2 = Electrolytic Capacitor [capacitance=1µF package="100 mil [THT, electrolytic]"]
  JACK1 = 2.1mm Barrel Jack with Terminal Block
  JP1 = Header 4 [package=screwterminal-3.5mm-4_lock]
  JP2 = Header 4 [package=screwterminal-3.5mm-4_lock]
  MCU1 = Raspberry Pi Zero  # not connected

nets:
  VDD: Part1.5V, Pololu_A1.VDD, Pololu_A2.VDD
  N1: Part1.D22, Pololu_A1.DIR
  N2: Part1.D24, Pololu_A1.STEP
  N3: Part1.D26, Pololu_A1.MS3
  N4: Part1.D28, Pololu_A1.MS2
  N5: Part1.D30, Pololu_A1.MS1
  N6: Part1.D32, Pololu_A1.ENABLE
  N7: Part1.D42, Pololu_A2.DIR
  N8: Part1.D44, Pololu_A2.STEP
  N9: Part1.D46, Pololu_A2.MS3
  N10: Part1.D48, Pololu_A2.MS2
  N11: Part1.D50, Pololu_A2.MS1
  N12: Part1.D52, Pololu_A2.ENABLE
  N13: Part1.GND, Pololu_A1.GND#8, Pololu_A2.GND#8
  N14: Pololu_A1.RESET, Pololu_A1.SLEEP
  N15: Pololu_A1.1B, JP1.1
  N16: Pololu_A1.1A, JP1.2
  N17: Pololu_A1.2A, JP1.3
  N18: Pololu_A1.2B, JP1.4
  N19: Pololu_A1.GND#14, Pololu_A2.GND#14, C1.-, C2.-, JACK1.NEG
  N20: Pololu_A1.VMOT, Pololu_A2.VMOT, C1.+, C2.+, JACK1.POS
  N21: Pololu_A2.RESET, Pololu_A2.SLEEP
  N22: Pololu_A2.1B, JP2.1
  N23: Pololu_A2.1A, JP2.2
  N24: Pololu_A2.2A, JP2.3
  N25: Pololu_A2.2B, JP2.4
